// Logisim project calculator.circ as structural Verilog: 7 circuits, main circuit main
module main (
  input  A0,
  input  A1,
  input  AS,
  input  B0,
  input  B1,
  input  BS,
  input  S1,
  input  S2,
  output ZERO_FLAG,
  output out_10
);

  wire add_sub_1_c0, add_sub_1_c1, add_sub_1_c2, add_sub_1_sign, and_1_out, and_2_out, M_c0, M_c1, M_c2,
       M_c3, M_sign, multiplexor_4bit_1_output, multiplexor_4bit_2_output, multiplexor_4bit_3_output,
       multiplexor_4bit_4_output, n7_segment_1_a_2, n7_segment_1_b_2, n7_segment_1_c_2, n7_segment_1_d_2,
       n7_segment_1_e_2, n7_segment_1_f, n7_segment_1_g, not_1_out, or_1_out, or_2_out, reminder_div_0,
       reminder_r0, reminder_r1, reminder_s;

  multiplier M (
    .As(AS), .Bs(BS), .A0(A0), .A1(A1), .B0(B0), .B1(B1), .Sign(M_sign), .C0(M_c0), .C1(M_c1), .C2(M_c2),
    .C3(M_c3));
  add_sub add_sub_1 (
    .a0(A0), .a1(A1), .as(AS), .b0(B0), .b1(B1), .bs(BS), .op0(S2), .C0(add_sub_1_c0), .C1(add_sub_1_c1),
    .C2(add_sub_1_c2), .sign(add_sub_1_sign));
  reminder reminder (
    .as(AS), .a0(A0), .a1(A1), .b0(B0), .b1(B1), .s(reminder_s), .r0(reminder_r0), .r1(reminder_r1),
    .div_0(reminder_div_0));
  multiplexor_4bit multiplexor_4bit_1 (
    .First(reminder_r0), .Second(add_sub_1_c0), .Third(add_sub_1_c0), .Fourth(M_c0), .Selector_1(S1),
    .Selector_2(S2), .Output(multiplexor_4bit_1_output));
  multiplexor_4bit multiplexor_4bit_2 (
    .First(reminder_r1), .Second(add_sub_1_c1), .Third(add_sub_1_c1), .Fourth(M_c1), .Selector_1(S1),
    .Selector_2(S2), .Output(multiplexor_4bit_2_output));
  multiplexor_4bit multiplexor_4bit_3 (
    .First(1'b0), .Second(add_sub_1_c2), .Third(add_sub_1_c2), .Fourth(M_c2), .Selector_1(S1),
    .Selector_2(S2), .Output(multiplexor_4bit_3_output));
  and and_1 (and_1_out, M_c3, S1, S2);
  multiplexor_4bit multiplexor_4bit_4 (
    .First(reminder_s), .Second(add_sub_1_sign), .Third(add_sub_1_sign), .Fourth(M_sign), .Selector_1(S1),
    .Selector_2(S2), .Output(multiplexor_4bit_4_output));
  not not_1 (not_1_out, reminder_div_0);
  or or_1 (or_1_out, not_1_out, S1, S2);
  _7_segment u_7_segment_1 (
    .E(or_1_out), .D(and_1_out), .C(multiplexor_4bit_3_output), .B(multiplexor_4bit_2_output),
    .A(multiplexor_4bit_1_output), .a_2(n7_segment_1_a_2), .b_2(n7_segment_1_b_2), .c_2(n7_segment_1_c_2),
    .d_2(n7_segment_1_d_2), .e_2(n7_segment_1_e_2), .f(n7_segment_1_f), .g(n7_segment_1_g));
  not not_2 (out_10, or_1_out);
  or or_2 (or_2_out, multiplexor_4bit_1_output, multiplexor_4bit_2_output, out_10, multiplexor_4bit_3_output, and_1_out);
  // Simple_buzzer simple_buzzer_1: pin names not known; wires that end beside it: out_10
  and and_2 (and_2_out, or_1_out, or_2_out, multiplexor_4bit_4_output);
  not not_3 (ZERO_FLAG, or_2_out);
  _7_Segment_Display u_7_segment_display_1 (
    .g(n7_segment_1_g), .f(n7_segment_1_f), .a(n7_segment_1_a_2), .b(n7_segment_1_b_2), .e(n7_segment_1_e_2),
    .d(n7_segment_1_d_2), .c(n7_segment_1_c_2));  // open: dp
  _7_Segment_Display u_7_segment_display_2 (.g(and_2_out));  // open: f, a, b, e, d, c, dp

  // Notes on the sheet:
  //   (0,0)->Reminder
  //   (1,0)->addition
  //   (0,1)->subtraction
  //   (1,1)->Multiplication
  //   A/S
  //   C0
  //   C1
  //   C2
  //   C3
  //   S
  //   2
  //   2
  //   4
  //   2
  //   DIV BY ZERO FLAG AND BUZZER
endmodule

module reminder (
  input  as,
  input  a0,
  input  a1,
  input  b0,
  input  b1,
  output s,
  output r0,
  output r1,
  output div_0
);

  wire [1:0] priority_encoder_1_out;
  wire [1:1] xor_1_out;
  wire [3:0] adder_1_out, adder_2_out, adder_3_out;

  xor xor_1 (xor_1_out[1], b0, b1);
  nor nor_1 (div_0, b1, b0);
  Adder #(.width(4)) adder_1 (
    .a({2'b00, a1, a0}), .b({2'b11, xor_1_out[1], b0}), .out(adder_1_out));  // open: cin, cout
  Adder #(.width(4)) adder_2 (.a(adder_1_out), .b({2'b11, xor_1_out[1], b0}), .out(adder_2_out));  // open: cin, cout
  Adder #(.width(4)) adder_3 (.a(adder_2_out), .b({2'b11, xor_1_out[1], b0}), .out(adder_3_out));  // open: cin, cout
  Priority_Encoder #(.select(2)) priority_encoder_1 (
    .in0(1'b1), .in1(adder_3_out[3]), .in2(adder_2_out[3]), .in3(adder_1_out[3]), .out(priority_encoder_1_out));  // open: gs, en_out, en_in
  Multiplexer #(.select(2), .width(2), .enable("false")) multiplexer_1 (
    .in0(adder_3_out[1:0]), .in1(adder_2_out[1:0]), .in2(adder_1_out[1:0]), .in3({a1, a0}), .out({r1, r0}),
    .sel(priority_encoder_1_out));

  assign s = as;
endmodule

module adder (
  input  ao,
  input  b0,
  input  b1,
  input  a1,
  input  b2,
  input  a2,
  input  b3,
  input  a3,
  output s1,
  output s2,
  output s3,
  output s4,
  output carry
);

  wire and_1_out, and_2_out, and_3_out, and_4_out, and_5_out, and_6_out, and_7_out, and_8_out, and_9_out,
       and_10_out, or_1_out, or_2_out, or_3_out, or_4_out, or_5_out, xor_2_out, xor_3_out, xor_5_out;

  xor xor_1 (s1, ao, b0);
  and and_1 (and_1_out, ao, b0);
  xor xor_2 (xor_2_out, b1, a1);
  xor xor_3 (xor_3_out, b2, a2);
  xor xor_4 (s2, and_1_out, xor_2_out);
  xor xor_5 (xor_5_out, b3, a3);
  and and_2 (and_2_out, and_1_out, a1);
  and and_3 (and_3_out, a1, b1);
  and and_4 (and_4_out, and_1_out, b1);
  xor xor_6 (s3, or_4_out, xor_3_out);
  and and_5 (and_5_out, or_4_out, a2);
  and and_6 (and_6_out, a2, b2);
  and and_7 (and_7_out, or_4_out, b2);
  xor xor_7 (s4, or_3_out, xor_5_out);
  and and_8 (and_8_out, or_3_out, a3);
  and and_9 (and_9_out, a3, b3);
  and and_10 (and_10_out, or_3_out, b3);
  or or_1 (or_1_out, and_2_out, and_3_out);
  or or_2 (or_2_out, and_5_out, and_6_out);
  or or_3 (or_3_out, or_2_out, and_7_out);
  or or_4 (or_4_out, or_1_out, and_4_out);
  or or_5 (or_5_out, and_8_out, and_9_out);
  or or_6 (carry, or_5_out, and_10_out);

  // Notes on the sheet:
  //   7 xor
  //   10 and
  //   6 OR
  //   c1
  //   c2
  //   c3
endmodule

module add_sub (
  input  a0,
  input  a1,
  input  as,
  input  b0,
  input  b1,
  input  bs,
  input  op0,
  output C0,
  output C1,
  output C2,
  output sign
);

  wire _1_0_out, _01_2_out, _01_3_out, _01_4_out, _01_out, _1_prime_0_out, _2_prime_out, adder_1_s2,
       adder_1_s3, multiplexer_1_out, multiplexer_2_out, s_2_out, s_out, sign_out;

  xor u_sign (sign_out, bs, op0);
  xor _01 (_01_out, a0, a1);
  and s (s_out, as, _01_2_out);
  or _01_2 (_01_2_out, a1, a0);
  xor _01_3 (_01_3_out, b0, b1);
  and s_2 (s_2_out, sign_out, _01_4_out);
  or _01_4 (_01_4_out, b1, b0);
  Multiplexer #(.enable("false")) multiplexer_1 (.in0(a1), .in1(_01_out), .out(multiplexer_1_out), .sel(s_out));
  Multiplexer #(.enable("false")) multiplexer_2 (.in0(b1), .in1(_01_3_out), .out(multiplexer_2_out), .sel(s_2_out));
  adder adder_1 (
    .ao(a0), .b0(b0), .b1(multiplexer_2_out), .a1(multiplexer_1_out), .b2(s_2_out), .a2(s_out), .b3(s_2_out),
    .a3(s_out), .s1(C0), .s2(adder_1_s2), .s3(adder_1_s3), .s4(sign));  // open: carry
  or _1_0 (_1_0_out, C0, adder_1_s2);
  xor _1_prime_0 (_1_prime_0_out, adder_1_s2, C0);
  xor _2_prime (_2_prime_out, _1_0_out, adder_1_s3);
  Multiplexer #(.enable("false")) multiplexer_3 (.in0(adder_1_s2), .in1(_1_prime_0_out), .out(C1), .sel(sign));
  Multiplexer #(.enable("false")) multiplexer_4 (.in0(adder_1_s3), .in1(_2_prime_out), .out(C2), .sel(sign));

  // Notes on the sheet:
  //   2nd Compliment
  //   2nd Compliment
  //   2 and - 1 or
  //   Selecting complement if negative
  //   Selecting complement if negative
  //   adding
  //   know the sign from third or fouth bit
  //   most efficient
  //   5 xor 2
  //   4 or 1
  //   2 and 1
  //   2nd Compliment
  //   4 multiplex
  //   1 adder
  //   Selecting complement if negative
endmodule

module multiplier (
  input  As,
  input  Bs,
  input  A0,
  input  A1,
  input  B0,
  input  B1,
  output Sign,
  output C0,
  output C1,
  output C2,
  output C3
);

  wire and_1_out, and_2_out, and_3_out, and_4_out;

  xor xor_1 (Sign, As, Bs);
  and and_1 (and_1_out, A0, B1);
  and and_2 (and_2_out, A1, B0);
  and and_3 (and_3_out, A1, B1);
  xor xor_2 (C1, and_1_out, and_2_out);
  and and_4 (and_4_out, and_1_out, and_2_out);
  xor xor_3 (C2, and_3_out, and_4_out);
  and and_5 (C3, and_3_out, and_4_out);
  and and_6 (C0, A0, B0);

  // Notes on the sheet:
  //   o +ve / 1-ve
endmodule

module multiplexor_4bit (
  input  First,
  input  Second,
  input  Third,
  input  Fourth,
  input  Selector_1,
  input  Selector_2,
  output Output
);

  wire nand_1_out, nand_2_out, nand_3_out, nand_4_out, not_1_out, not_2_out;

  not not_1 (not_1_out, Selector_1);
  not not_2 (not_2_out, Selector_2);
  nand nand_1 (nand_1_out, Third, not_2_out, Selector_1);
  nand nand_2 (nand_2_out, Fourth, Selector_1, Selector_2);
  nand nand_3 (nand_3_out, First, not_1_out, not_2_out);
  nand nand_4 (nand_4_out, Second, not_1_out, Selector_2);
  nand nand_5 (Output, nand_3_out, nand_4_out, nand_1_out, nand_2_out);

  // Notes on the sheet:
  //   (0,0)->First
  //   (0,1)->Second
  //   (1,0)->Third
  //   (1,1)->Fourth
endmodule

module _7_segment (
  input  E,
  input  D,
  input  C,
  input  B,
  input  A,
  output a_2,
  output b_2,
  output c_2,
  output d_2,
  output e_2,
  output f,
  output g
);

  wire nand_1_out, nand_2_out, nand_3_out, nand_4_out, nand_5_out, nand_6_out, nand_7_out, nand_8_out,
       nand_9_out, nand_10_out, nand_11_out, nand_12_out, nand_13_out, nand_14_out, nand_15_out, nand_16_out,
       nand_17_out, nand_18_out, nand_19_out, nand_20_out, nand_21_out, nand_22_out, nand_23_out,
       nand_24_out, nand_25_out, nand_26_out, nand_27_out, nand_28_out, nand_29_out, nand_30_out,
       nand_31_out, nand_32_out, nand_33_out, nand_34_out, nand_35_out, nand_36_out, nand_37_out,
       nand_38_out, nand_39_out, nand_40_out, nand_41_out, nand_42_out, nand_43_out, nand_44_out,
       nand_45_out, nand_46_out, nand_47_out, nand_48_out, nand_49_out, nand_50_out, nand_51_out,
       nand_52_out, nand_53_out, nand_54_out, nand_55_out, nand_56_out, nand_57_out, nand_58_out,
       nand_59_out, nand_60_out, nand_61_out, nand_62_out, nand_63_out, nand_64_out, nand_65_out,
       nand_66_out, nand_67_out, nand_68_out, nand_69_out, nand_70_out, nand_71_out, nand_72_out,
       nand_73_out, nand_74_out, nand_75_out, nand_76_out, nand_77_out, nand_78_out, nand_79_out,
       nand_80_out, nand_81_out, nand_82_out, nand_83_out, nand_84_out, nand_85_out, nand_86_out,
       nand_87_out, nand_88_out, nand_89_out, nand_90_out, nand_91_out, nand_92_out, nand_93_out,
       nand_94_out, nand_95_out, nand_96_out, nand_97_out, nand_98_out, nand_99_out, nand_100_out,
       nand_101_out, nand_102_out, nand_103_out, nand_104_out, nand_105_out, nand_106_out, nand_107_out,
       nand_108_out, nand_109_out, nand_110_out, nand_111_out, nand_112_out, nand_113_out, nand_114_out,
       nand_115_out, nand_116_out, nand_117_out, nand_118_out, nand_119_out, nand_120_out, nand_121_out,
       nand_122_out, nand_123_out, nand_124_out, nand_125_out, nand_126_out, nand_127_out, nand_128_out,
       nand_129_out, nand_130_out, nand_131_out, nand_132_out, nand_133_out, nand_134_out, nand_135_out,
       nand_136_out, nand_137_out, nand_138_out, nand_139_out, nand_140_out, nand_141_out, nand_142_out,
       nand_143_out, nand_144_out, nand_145_out, nand_146_out, nand_147_out, nand_148_out, nand_149_out,
       nand_150_out, nand_151_out, nand_152_out;

  nand nand_1 (nand_1_out, C, C);
  nand nand_2 (nand_2_out, D, D);
  nand nand_3 (nand_3_out, B, B);
  nand nand_4 (nand_4_out, D, D);
  nand nand_5 (nand_5_out, B, B);
  nand nand_6 (nand_6_out, D, D);
  nand nand_7 (nand_7_out, D, D);
  nand nand_8 (nand_8_out, C, C);
  nand nand_9 (nand_9_out, C, C);
  nand nand_10 (nand_10_out, C, C);
  nand nand_11 (nand_11_out, A, A);
  nand nand_12 (nand_12_out, A, A);
  nand nand_13 (nand_13_out, D, D);
  nand nand_14 (nand_14_out, C, C);
  nand nand_15 (nand_15_out, A, A);
  nand nand_16 (nand_16_out, D, D);
  nand nand_17 (nand_17_out, D, nand_1_out);
  nand nand_18 (nand_18_out, nand_2_out, nand_3_out);
  nand nand_19 (nand_19_out, nand_4_out, nand_5_out);
  nand nand_20 (nand_20_out, nand_6_out, A);
  nand nand_21 (nand_21_out, nand_7_out, nand_8_out);
  nand nand_22 (nand_22_out, nand_9_out, B);
  nand nand_23 (nand_23_out, nand_10_out, nand_11_out);
  nand nand_24 (nand_24_out, B, nand_12_out);
  nand nand_25 (nand_25_out, D, B);
  nand nand_26 (nand_26_out, D, C);
  nand nand_27 (nand_27_out, nand_13_out, C);
  nand nand_28 (nand_28_out, nand_14_out, B);
  nand nand_29 (nand_29_out, B, nand_15_out);
  nand nand_30 (nand_30_out, nand_16_out, C);
  nand nand_31 (nand_31_out, C, C);
  nand nand_32 (nand_32_out, A, A);
  nand nand_33 (nand_33_out, D, D);
  nand nand_34 (nand_34_out, D, D);
  nand nand_35 (nand_35_out, nand_17_out, nand_17_out);
  nand nand_36 (nand_36_out, B, B);
  nand nand_37 (nand_37_out, D, D);
  nand nand_38 (nand_38_out, C, C);
  nand nand_39 (nand_39_out, nand_18_out, nand_18_out);
  nand nand_40 (nand_40_out, A, A);
  nand nand_41 (nand_41_out, D, D);
  nand nand_42 (nand_42_out, B, B);
  nand nand_43 (nand_43_out, nand_19_out, nand_20_out);
  nand nand_44 (nand_44_out, B, B);
  nand nand_45 (nand_45_out, D, D);
  nand nand_46 (nand_46_out, C, C);
  nand nand_47 (nand_47_out, nand_21_out, nand_21_out);
  nand nand_48 (nand_48_out, A, A);
  nand nand_49 (nand_49_out, nand_22_out, nand_22_out);
  nand nand_50 (nand_50_out, B, B);
  nand nand_51 (nand_51_out, B, B);
  nand nand_52 (nand_52_out, nand_23_out, nand_24_out);
  nand nand_53 (nand_53_out, nand_25_out, nand_26_out);
  nand nand_54 (nand_54_out, B, B);
  nand nand_55 (nand_55_out, A, A);
  nand nand_56 (nand_56_out, nand_27_out, nand_27_out);
  nand nand_57 (nand_57_out, B, B);
  nand nand_58 (nand_58_out, nand_28_out, nand_29_out);
  nand nand_59 (nand_59_out, nand_30_out, nand_30_out);
  nand nand_60 (nand_60_out, B, B);
  nand nand_61 (nand_61_out, C, C);
  nand nand_62 (nand_62_out, nand_31_out, nand_32_out);
  nand nand_63 (nand_63_out, nand_33_out, B);
  nand nand_64 (nand_64_out, nand_34_out, C);
  nand nand_65 (nand_65_out, C, B);
  nand nand_66 (nand_66_out, nand_35_out, nand_36_out);
  nand nand_67 (nand_67_out, nand_37_out, nand_38_out);
  nand nand_68 (nand_68_out, nand_39_out, nand_40_out);
  nand nand_69 (nand_69_out, nand_41_out, B);
  nand nand_70 (nand_70_out, D, nand_42_out);
  nand nand_71 (nand_71_out, nand_43_out, nand_43_out);
  nand nand_72 (nand_72_out, nand_44_out, A);
  nand nand_73 (nand_73_out, nand_45_out, C);
  nand nand_74 (nand_74_out, D, nand_46_out);
  nand nand_75 (nand_75_out, nand_47_out, nand_48_out);
  nand nand_76 (nand_76_out, nand_49_out, A);
  nand nand_77 (nand_77_out, C, nand_50_out);
  nand nand_78 (nand_78_out, C, B);
  nand nand_79 (nand_79_out, D, nand_51_out);
  nand nand_80 (nand_80_out, nand_52_out, nand_52_out);
  nand nand_81 (nand_81_out, nand_53_out, nand_53_out);
  nand nand_82 (nand_82_out, nand_54_out, nand_55_out);
  nand nand_83 (nand_83_out, nand_56_out, nand_57_out);
  nand nand_84 (nand_84_out, nand_58_out, nand_58_out);
  nand nand_85 (nand_85_out, nand_59_out, nand_60_out);
  nand nand_86 (nand_86_out, D, nand_61_out);
  nand nand_87 (nand_87_out, D, A);
  nand nand_88 (nand_88_out, nand_62_out, nand_63_out);
  nand nand_89 (nand_89_out, nand_64_out, nand_64_out);
  nand nand_90 (nand_90_out, nand_65_out, nand_66_out);
  nand nand_91 (nand_91_out, A, A);
  nand nand_92 (nand_92_out, nand_67_out, nand_68_out);
  nand nand_93 (nand_93_out, C, C);
  nand nand_94 (nand_94_out, A, A);
  nand nand_95 (nand_95_out, nand_69_out, nand_69_out);
  nand nand_96 (nand_96_out, nand_70_out, nand_70_out);
  nand nand_97 (nand_97_out, nand_71_out, nand_72_out);
  nand nand_98 (nand_98_out, nand_73_out, nand_74_out);
  nand nand_99 (nand_99_out, nand_75_out, nand_76_out);
  nand nand_100 (nand_100_out, nand_77_out, nand_77_out);
  nand nand_101 (nand_101_out, nand_78_out, nand_78_out);
  nand nand_102 (nand_102_out, A, A);
  nand nand_103 (nand_103_out, nand_79_out, nand_79_out);
  nand nand_104 (nand_104_out, A, A);
  nand nand_105 (nand_105_out, nand_80_out, nand_81_out);
  nand nand_106 (nand_106_out, nand_82_out, nand_83_out);
  nand nand_107 (nand_107_out, A, A);
  nand nand_108 (nand_108_out, C, C);
  nand nand_109 (nand_109_out, nand_84_out, nand_85_out);
  nand nand_110 (nand_110_out, nand_86_out, nand_87_out);
  nand nand_111 (nand_111_out, nand_88_out, nand_88_out);
  nand nand_112 (nand_112_out, nand_89_out, A);
  nand nand_113 (nand_113_out, nand_90_out, nand_90_out);
  nand nand_114 (nand_114_out, D, nand_91_out);
  nand nand_115 (nand_115_out, nand_92_out, nand_92_out);
  nand nand_116 (nand_116_out, nand_93_out, nand_94_out);
  nand nand_117 (nand_117_out, nand_95_out, A);
  nand nand_118 (nand_118_out, nand_96_out, A);
  nand nand_119 (nand_119_out, nand_97_out, nand_97_out);
  nand nand_120 (nand_120_out, nand_98_out, nand_98_out);
  nand nand_121 (nand_121_out, nand_99_out, nand_99_out);
  nand nand_122 (nand_122_out, nand_100_out, A);
  nand nand_123 (nand_123_out, nand_101_out, nand_102_out);
  nand nand_124 (nand_124_out, nand_103_out, nand_104_out);
  nand nand_125 (nand_125_out, nand_106_out, nand_106_out);
  nand nand_126 (nand_126_out, C, nand_107_out);
  nand nand_127 (nand_127_out, D, nand_108_out);
  nand nand_128 (nand_128_out, D, B);
  nand nand_129 (nand_129_out, nand_109_out, nand_109_out);
  nand nand_130 (nand_130_out, nand_110_out, nand_110_out);
  nand nand_131 (nand_131_out, nand_111_out, nand_112_out);
  nand nand_132 (nand_132_out, nand_113_out, nand_114_out);
  nand nand_133 (nand_133_out, nand_115_out, nand_116_out);
  nand nand_134 (nand_134_out, nand_117_out, nand_118_out);
  nand nand_135 (nand_135_out, nand_119_out, nand_120_out);
  nand nand_136 (nand_136_out, nand_121_out, nand_122_out);
  nand nand_137 (nand_137_out, nand_123_out, nand_124_out);
  nand nand_138 (nand_138_out, nand_125_out, nand_126_out);
  nand nand_139 (nand_139_out, nand_127_out, nand_128_out);
  nand nand_140 (nand_140_out, nand_129_out, nand_130_out);
  nand nand_141 (nand_141_out, nand_131_out, nand_131_out);
  nand nand_142 (nand_142_out, nand_132_out, nand_132_out);
  nand nand_143 (nand_143_out, nand_133_out, nand_133_out);
  nand nand_144 (nand_144_out, nand_134_out, nand_134_out);
  nand nand_145 (nand_145_out, nand_136_out, nand_136_out);
  nand nand_146 (nand_146_out, nand_137_out, nand_137_out);
  nand nand_147 (nand_147_out, nand_138_out, nand_138_out);
  nand nand_148 (nand_148_out, nand_139_out, nand_139_out);
  nand nand_149 (nand_149_out, nand_141_out, nand_142_out);
  nand nand_150 (nand_150_out, nand_143_out, nand_144_out);
  nand nand_151 (nand_151_out, nand_145_out, nand_146_out);
  nand nand_152 (nand_152_out, nand_147_out, nand_148_out);
  and and_1 (b_2, E, nand_150_out);
  and and_2 (c_2, E, nand_135_out);
  and and_3 (d_2, E, nand_151_out);
  and and_4 (e_2, E, nand_105_out);
  and and_5 (f, E, nand_152_out);
  and and_6 (g, E, nand_140_out);
  and and_7 (a_2, E, nand_149_out);
endmodule
